# Fritzing sketch trigger_nirs (saved by Fritzing 0.9.2b)
circuit board: 6.55996cm x 4.32948cm
breadboards: 1

parts:
  LED1 = LED - 5mm [color="Green (565nm)" package="5 mm [THT]"]
  R1 = Resistor [tolerance=±5% resistance=330 package=THT]
  R2 = Resistor [tolerance=±5% resistance=330 package=THT]
  R3 = Resistor [tolerance=±5% resistance=330 package=THT]
  R4 = Resistor [tolerance=±5% resistance=330 package=THT]
  R5 = Resistor [tolerance=±5% resistance=330 package=THT]
  Componente3 = DB25F
  Componente2 = Arduino Nano (Rev3.0)

nets:
  N1: LED1.cathode, Componente3.pin10, Componente2.GND
  N2: LED1.anode, R1.Pin_0
  N3: R1.Pin_1, Componente2.D13/SCK
  N4: R2.Pin_0, Componente3.pin5
  N5: R2.Pin_1, Componente2.D2
  N6: R3.Pin_0, Componente3.pin4
  N7: R3.Pin_1, Componente2.D3
  N8: R4.Pin_0, Componente3.pin3
  N9: R4.Pin_1, Componente2.D4
  N10: R5.Pin_0, Componente3.pin2
  N11: R5.Pin_1, Componente2.D5
